# Fritzing sketch iotca2 (saved by Fritzing 0.9.3b)
breadboards: 1

parts:
  IC1 = MCP3008 8-channel 10-bit ADC [part_number=MCP3008]  # not connected
  Part2 = HC-SR501 Body Sensor Module
  LED1 = LEDs [package=led10mm]
  R3 = Resistor [tolerance=±5% resistance=220 package="2010 [SMD]"]
  Part1 = Adafruit T-Cobbler Plus [part_number="Adafruit #1989 and #2028"]

nets:
  N1: Part2.VCC, Part1.+3.3V_2
  N2: Part2.OUT, Part1.GPIO21
  GND: Part2.GND, R3.Pin_0, Part1.GND
  N3: LED1.C, R3.Pin_1
  N4: LED1.A, Part1.GPIO23

notes:
  Cable Information
  -------------------------
  Red - 5 Volts
  Black - GND (Ground)
  Yellow - GPIO Jumper Cable
  Orange - MCP3008 Jumper Cable

custom parts:
  HC-SR501 Body Sensor Module: Pyroelectric Infrared PIR Motion Sensor Detector Module
  Adafruit T-Cobbler Plus: The Raspberry Pi has landed on the Maker World like a 40-GPIO pinned, quad-USB ported, credit card sized bomb of DIY joy. And while you can use most of our great Model B accessories by hooking up our downgrade cable, its probably a good time to upgrade your set up and accessorize using all of the 40 pins. That's why we now carry the Assembled Adafruit Pi T-Cobbler Plus - Breakout + Cable for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
